// Logisim project project.circ as structural Verilog: 9 circuits, main circuit main
module main (
);

  wire alu_1_zeroflag, armux2, Clock, control_unit_1_armux, control_unit_1_irload, control_unit_1_memload,
       control_unit_1_pc_plus_plus, control_unit_1_pcload, control_unit_1_regload, control_unit_1_zfld, mux0,
       mux1, not_1_out, register_1_q;
  wire [2:0] irload_1_alucode, irload_1_destination___src1, irload_1_src2, irload_1_src3;
  wire [3:0] ram_1_data_2;
  wire [11:0] adder_1_out, adder_2_out, irload_1__12bitaddr, multiplexer_1_out, multiplexer_2_out,
       pc_1_pcout, ram_1_data;
  wire [15:0] alu_1_out, multiplexer_3_out, multiplexer_4_out, registerbank_1_d0, registerbank_1_d1,
       registerbank_1_d2, registerbank_1_d3, registerbank_1_d4, registerbank_1_d5, registerbank_1_d6,
       registerbank_1_d7, rin;

  Adder #(.width(12)) adder_1 (.a(pc_1_pcout), .b(irload_1__12bitaddr), .out(adder_1_out));  // open: cin, cout
  Clock clock_1 (.out(Clock));
  Adder #(.width(12)) adder_2 (.a(pc_1_pcout), .b(multiplexer_4_out[11:0]), .out(adder_2_out));  // open: cin, cout
  Multiplexer #(.width(12), .enable("false")) multiplexer_1 (
    .in0(adder_1_out), .in1(adder_2_out), .out(multiplexer_1_out), .sel(armux2));
  PC pc_1 (
    .PCIN(multiplexer_1_out), .pcload(control_unit_1_pcload), .clk(Clock),
    .pc_plus_plus(control_unit_1_pc_plus_plus), .PCOUT(pc_1_pcout));
  Control_Unit control_unit_1 (
    .OPCODE(ram_1_data_2), .zf(register_1_q), .clk(Clock), .PCLOAD(control_unit_1_pcload),
    .PC_plus_plus(control_unit_1_pc_plus_plus), .ARMUX(control_unit_1_armux),
    .REGLOAD(control_unit_1_regload), .ZFLD(control_unit_1_zfld), .MUX1(mux1), .MUX0(mux0),
    .IRLOAD(control_unit_1_irload), .memload(control_unit_1_memload), .armux2(armux2));  // open: fetch
  Multiplexer #(.width(12), .enable("false")) multiplexer_2 (
    .in0(pc_1_pcout), .in1(multiplexer_4_out[11:0]), .out(multiplexer_2_out), .sel(control_unit_1_armux));
  not not_1 (not_1_out, control_unit_1_memload);
  RAM #(.addrWidth(12), .dataWidth(16), .bus("separate")) ram_1 (
    .addr(multiplexer_2_out), .din(rin), .data({ram_1_data_2, ram_1_data}), .str(control_unit_1_memload),
    .clk(Clock), .ld(not_1_out));  // open: sel, clr
  RegisterBank registerbank_1 (
    .clk(Clock), .D0(registerbank_1_d0), .D1(registerbank_1_d1), .D2(registerbank_1_d2),
    .D3(registerbank_1_d3), .D4(registerbank_1_d4), .D5(registerbank_1_d5), .D6(registerbank_1_d6),
    .D7(registerbank_1_d7), .regSelect(irload_1_destination___src1), .Din(rin),
    .regwrt(control_unit_1_regload));
  IRLOAD irload_1 (
    .in(ram_1_data), ._12bitAddr(irload_1__12bitaddr), .DESTINATION___SRC1(irload_1_destination___src1),
    .SRC3(irload_1_src3), .SRC2(irload_1_src2), .aluCode(irload_1_alucode), .IRLD(control_unit_1_irload),
    .clk(Clock));
  Register #(.width(1)) register_1 (
    .D(alu_1_zeroflag), .en(control_unit_1_zfld), .Q(register_1_q), .clk(Clock));  // open: clr
  Multiplexer #(.select(3), .width(16), .enable("false")) multiplexer_3 (
    .in0(registerbank_1_d0), .in1(registerbank_1_d1), .in2(registerbank_1_d2), .in3(registerbank_1_d3),
    .in4(registerbank_1_d4), .in5(registerbank_1_d5), .in6(registerbank_1_d6), .in7(registerbank_1_d7),
    .out(multiplexer_3_out), .sel(irload_1_src2));
  Multiplexer #(.select(3), .width(16), .enable("false")) multiplexer_4 (
    .in0(registerbank_1_d0), .in1(registerbank_1_d1), .in2(registerbank_1_d2), .in3(registerbank_1_d3),
    .in4(registerbank_1_d4), .in5(registerbank_1_d5), .in6(registerbank_1_d6), .in7(registerbank_1_d7),
    .out(multiplexer_4_out), .sel(irload_1_src3));
  ALU alu_1 (
    .op1(multiplexer_4_out), .op2(multiplexer_3_out), .aluOP1(irload_1_alucode), .zeroflag(alu_1_zeroflag),
    .aluOP2(irload_1_src2), .out(alu_1_out));
  Multiplexer #(.select(2), .width(16), .enable("false")) multiplexer_5 (
    .in0({ram_1_data_2, ram_1_data}), .in1(multiplexer_3_out), .in2(multiplexer_4_out), .in3(alu_1_out),
    .out(rin), .sel({mux1, mux0}));
endmodule

// REGBANK
module RegisterBank (
  input  clk,
  input  regwrt,
  input  [2:0] regSelect,
  input  [15:0] Din,
  output [15:0] D0,
  output [15:0] D1,
  output [15:0] D2,
  output [15:0] D3,
  output [15:0] D4,
  output [15:0] D5,
  output [15:0] D6,
  output [15:0] D7
);

  wire and_1_out, and_2_out, and_3_out, and_4_out, and_5_out, and_6_out, and_7_out, and_8_out,
       decoder_1_out0, decoder_1_out1, decoder_1_out2, decoder_1_out3, decoder_1_out4, decoder_1_out5,
       decoder_1_out6, decoder_1_out7;

  Decoder #(.select(3)) decoder_1 (
    .out0(decoder_1_out0), .out1(decoder_1_out1), .out2(decoder_1_out2), .out3(decoder_1_out3),
    .out4(decoder_1_out4), .out5(decoder_1_out5), .out6(decoder_1_out6), .out7(decoder_1_out7),
    .sel(regSelect), .en(1'b1));
  and and_1 (and_1_out, decoder_1_out0, regwrt);
  and and_2 (and_2_out, decoder_1_out1, regwrt);
  and and_3 (and_3_out, decoder_1_out2, regwrt);
  and and_4 (and_4_out, decoder_1_out3, regwrt);
  and and_5 (and_5_out, decoder_1_out4, regwrt);
  and and_6 (and_6_out, decoder_1_out5, regwrt);
  and and_7 (and_7_out, decoder_1_out6, regwrt);
  and and_8 (and_8_out, decoder_1_out7, regwrt);
  _16__Bit_Reg u_16_bit_reg_1 (.Dout(D0), .clk(clk), .enable(and_1_out), .Din(Din));
  _16__Bit_Reg u_16_bit_reg_2 (.Dout(D1), .clk(clk), .enable(and_2_out), .Din(Din));
  _16__Bit_Reg u_16_bit_reg_3 (.Dout(D2), .clk(clk), .enable(and_3_out), .Din(Din));
  _16__Bit_Reg u_16_bit_reg_4 (.Dout(D3), .clk(clk), .enable(and_4_out), .Din(Din));
  _16__Bit_Reg u_16_bit_reg_5 (.Dout(D4), .clk(clk), .enable(and_5_out), .Din(Din));
  _16__Bit_Reg u_16_bit_reg_6 (.Dout(D5), .clk(clk), .enable(and_6_out), .Din(Din));
  _16__Bit_Reg u_16_bit_reg_7 (.Dout(D6), .clk(clk), .enable(and_7_out), .Din(Din));
  _16__Bit_Reg u_16_bit_reg_8 (.Dout(D7), .clk(clk), .enable(and_8_out), .Din(Din));
endmodule

module PC (
  input  [11:0] PCIN,
  input  pcload,
  input  clk,
  input  pc_plus_plus,
  output [11:0] PCOUT
);

  wire [11:0] adder_1_out, multiplexer_1_out, multiplexer_2_out;

  Multiplexer #(.width(12), .enable("false")) multiplexer_1 (
    .in0(adder_1_out), .in1(PCIN), .out(multiplexer_1_out), .sel(pcload));
  Register #(.width(12)) register_1 (.D(multiplexer_1_out), .Q(PCOUT), .clk(clk), .clr(1'b0));  // open: en
  Adder #(.width(12)) adder_1 (.a(multiplexer_2_out), .b(PCOUT), .out(adder_1_out));  // open: cin, cout
  Multiplexer #(.width(12), .enable("false")) multiplexer_2 (
    .in0({12{1'b0}}), .in1(12'h1), .out(multiplexer_2_out), .sel(pc_plus_plus));
endmodule

module ALU (
  input  [15:0] op1,
  input  [15:0] op2,
  input  [2:0] aluOP2,
  input  [2:0] aluOP1,
  output zeroflag,
  output [15:0] out
);

  wire and_2_out, or_2_out;
  wire [15:0] adder_1_out, adder_2_out, adder_3_out, adder_4_out, adder_5_out, and_1_out, multiplexer_1_out,
       multiplexer_3_out, not_1_out, not_2_out, or_1_out, xor_1_out;

  assign not_1_out = ~op2;  // NOT_Gate not_1, 16 bits wide
  assign and_1_out = op2 & op1;  // AND_Gate and_1, 16 bits wide
  assign or_1_out = op2 | op1;  // OR_Gate or_1, 16 bits wide
  assign xor_1_out = op2 ^ op1;  // XOR_Gate xor_1, 16 bits wide
  Adder #(.width(16)) adder_1 (.a(op2), .b(op1), .out(adder_1_out));  // open: cin, cout
  assign not_2_out = ~op1;  // NOT_Gate not_2, 16 bits wide
  and and_2 (and_2_out, aluOP1[0], aluOP1[1], aluOP1[2]);
  Adder #(.width(16)) adder_2 (.a(16'h1), .b(not_1_out), .out(adder_2_out));  // open: cin, cout
  Adder #(.width(16)) adder_3 (.a(adder_2_out), .b(op1), .out(adder_3_out));  // open: cin, cout
  Multiplexer #(.select(3), .width(16), .enable("false")) multiplexer_1 (
    .in0(adder_1_out), .in1(adder_3_out), .in2(and_1_out), .in3(or_1_out), .in4(xor_1_out),
    .out(multiplexer_1_out), .sel(aluOP1));  // open: in5, in6, in7
  Multiplexer #(.width(16), .enable("false")) multiplexer_2 (
    .in0(multiplexer_1_out), .in1(multiplexer_3_out), .out(out), .sel(and_2_out));
  Multiplexer #(.select(3), .width(16), .enable("false")) multiplexer_3 (
    .in0(not_2_out), .in1(op1), .in2(adder_5_out), .in3(adder_4_out), .out(multiplexer_3_out), .sel(aluOP2));  // open: in4, in5, in6, in7
  or or_2 (or_2_out, out[0], out[1], out[2], out[3], out[4], out[5], out[6], out[7], out[8], out[9], out[10], out[11], out[12], out[13], out[14], out[15]);
  Adder #(.width(16)) adder_4 (.a(op1), .b({16{1'b1}}), .out(adder_4_out));  // open: cin, cout
  Adder #(.width(16)) adder_5 (.a(op1), .b(16'h1), .out(adder_5_out));  // open: cin, cout
  not not_3 (zeroflag, or_2_out);

  // Notes on the sheet:
  //   and
  //   or
  //   xor
  //   add
  //   not
  //   sub
  //   dec
  //   inc
endmodule

module IRLOAD (
  input  [11:0] in,
  input  IRLD,
  input  clk,
  output [11:0] _12bitAddr,
  output [2:0] DESTINATION___SRC1,
  output [2:0] SRC3,
  output [2:0] SRC2,
  output [2:0] aluCode
);

  Register #(.width(12)) register_1 (.D(in), .en(IRLD), .Q(_12bitAddr), .clk(clk));  // open: clr

  assign aluCode = _12bitAddr[11:9];
  assign DESTINATION___SRC1 = _12bitAddr[2:0];
  assign SRC2 = _12bitAddr[8:6];
  assign SRC3 = _12bitAddr[5:3];
endmodule

// CONTROL UNIT
module Control_Unit (
  input  [3:0] OPCODE,
  input  zf,
  input  clk,
  output fetch,
  output IRLOAD,
  output armux2,
  output PCLOAD,
  output PC_plus_plus,
  output ARMUX,
  output REGLOAD,
  output ZFLD,
  output MUX1,
  output MUX0,
  output memload
);

  wire and_1_out, not_1_out, not_2_out, not_3_out, not_4_out;
  wire [1:0] and_2_out;
  wire [3:0] multiplexer_1_out, register_1_q;
  wire [15:11] rom_1_data;

  not not_1 (not_1_out, OPCODE[3]);
  and and_1 (and_1_out, not_1_out, OPCODE[2], not_3_out, not_2_out);
  and and_2 (and_2_out[0], fetch, zf, and_1_out);
  not not_2 (not_2_out, OPCODE[0]);
  not not_3 (not_3_out, OPCODE[1]);
  not not_4 (not_4_out, and_1_out);
  and and_3 (and_2_out[1], not_4_out, fetch);
  Multiplexer #(.select(2), .width(4), .enable("false")) multiplexer_1 (
    .in0(4'b0000), .in1(4'b0101), .in2(OPCODE), .out(multiplexer_1_out), .sel(and_2_out));  // open: in3
  Register #(.width(4)) register_1 (.D(multiplexer_1_out), .en(1'b1), .Q(register_1_q), .clk(clk), .clr(1'b0));
  ROM #(.addrWidth(4), .dataWidth(16)) rom_1 (
    .addr(register_1_q),
    .data({rom_1_data, fetch, armux2, PCLOAD, PC_plus_plus, ARMUX, REGLOAD, ZFLD, MUX1, MUX0, IRLOAD, memload}));  // open: sel

  // Notes on the sheet:
  //   contents of rom_1 (hex, n*v repeats v):
  //   482 a0 60 45 0 100 200 3c
endmodule

// 4-bit Reg
module _4_BIt_Reg (
  input  clk,
  input  enable,
  input  [3:0] din,
  output [3:0] dout
);

  wire not_1_out, not_2_out, not_3_out, not_4_out;

  not not_1 (not_1_out, din[3]);
  S_R_Flip_Flop s_r_ff_1 (
    .S(din[3]), .clk(clk), .R(not_1_out), .Q(dout[3]), .reset(1'b0), .en(enable));  // open: Qn, preset
  S_R_Flip_Flop s_r_ff_2 (
    .S(din[2]), .clk(clk), .R(not_2_out), .Q(dout[2]), .reset(1'b0), .en(enable));  // open: Qn, preset
  not not_2 (not_2_out, din[2]);
  not not_3 (not_3_out, din[1]);
  S_R_Flip_Flop s_r_ff_3 (
    .S(din[1]), .clk(clk), .R(not_3_out), .Q(dout[1]), .reset(1'b0), .en(enable));  // open: Qn, preset
  not not_4 (not_4_out, din[0]);
  S_R_Flip_Flop s_r_ff_4 (
    .S(din[0]), .clk(clk), .R(not_4_out), .Q(dout[0]), .reset(1'b0), .en(enable));  // open: Qn, preset
endmodule

module _16__Bit_Reg (
  input  clk,
  input  enable,
  input  [15:0] Din,
  output [15:0] Dout
);

  _4_BIt_Reg u_4_bit_reg_1 (.clk(clk), .enable(enable), .din(Din[3:0]), .dout(Dout[3:0]));
  _4_BIt_Reg u_4_bit_reg_2 (.clk(clk), .enable(enable), .din(Din[7:4]), .dout(Dout[7:4]));
  _4_BIt_Reg u_4_bit_reg_3 (.clk(clk), .enable(enable), .din(Din[11:8]), .dout(Dout[11:8]));
  _4_BIt_Reg u_4_bit_reg_4 (.clk(clk), .enable(enable), .din(Din[15:12]), .dout(Dout[15:12]));
endmodule

module _1Bit_Reg (
  input  in,
  input  LD,
  input  clk,
  output out
);

  wire and_1_out, and_2_out, not_1_out;

  not not_1 (not_1_out, in);
  and and_1 (and_1_out, in, LD);
  and and_2 (and_2_out, not_1_out, LD);
  S_R_Flip_Flop s_r_ff_1 (.S(and_1_out), .clk(clk), .R(and_2_out), .Q(out));  // open: Qn, preset, reset, en
endmodule
